# Fritzing sketch PhonicsBoardGame (saved by Fritzing 0.9.5d)
breadboards: 1

parts:
  DFPlayer_Mini1 = DFPlayer MINI [package="DIP (Dual Inline) [THT]"]
  Part1 = Arduino Uno (Rev3) - ICSP
  SP1 = SPEAKER [package=pcb_mount_speaker]
  S1 = Round Pushbutton
  S2 = Round Pushbutton
  S3 = Round Pushbutton
  S4 = Round Pushbutton
  S5 = Round Pushbutton
  S6 = Round Pushbutton
  S7 = Round Pushbutton
  S8 = Round Pushbutton
  S9 = Round Pushbutton
  S10 = Round Pushbutton
  S11 = Round Pushbutton
  S12 = Round Pushbutton
  S13 = Round Pushbutton
  S14 = Round Pushbutton
  S15 = Round Pushbutton
  S16 = Round Pushbutton
  S17 = Round Pushbutton
  S18 = Round Pushbutton
  S19 = Round Pushbutton
  S20 = Round Pushbutton
  S21 = Round Pushbutton
  S22 = Round Pushbutton
  S23 = Round Pushbutton
  S24 = Round Pushbutton
  S25 = Round Pushbutton
  S26 = Round Pushbutton
  S27 = Round Pushbutton
  S28 = Round Pushbutton
  S29 = Round Pushbutton
  S30 = Round Pushbutton
  DFPlayer_Mini2 = DFPlayer MINI [package="DIP (Dual Inline) [THT]"]
  SP2 = SPEAKER [package=pcb_mount_speaker]
  U1 = 4081 4 x 2 Input AND Gate, multi-part [part_number=4081 package="DIP (Dual Inline) [THT]"]  # not connected
  C1 = Electrolytic Capacitor [package="2cm H-Type"]

nets:
  VCC: DFPlayer_Mini1.VCC, Part1.5V
  N1: DFPlayer_Mini1.RX, Part1.D11_PWM/MOSI
  N2: DFPlayer_Mini1.TX, Part1.D10_PWM/SS
  N3: DFPlayer_Mini1.SPK1, SP1.-
  N4: DFPlayer_Mini1.SPK2, SP1.+
  GND: DFPlayer_Mini1.GND, Part1.GND, S5.leg0, S7.leg0, S15.leg0, S16.leg0, S29.leg0
  N5: Part1.D8, S2.leg0, S11.leg0, S19.leg0, S23.leg0, S26.leg0
  N6: Part1.D9_PWM, S4.leg0, S12.leg0, S14.leg0, S24.leg0, S25.leg0
  N7: Part1.D12/MISO, S3.leg0, S10.leg0, S18.leg0, S21.leg0, S30.leg0
  N8: Part1.D13/SCK, S6.leg0, S8.leg0, S13.leg0, S17.leg0, S28.leg0
  N9: Part1.D2, S25.leg1, S26.leg1, S27.leg1, S28.leg1, S29.leg1, S30.leg1
  N10: Part1.D3_PWM, S13.leg1, S14.leg1, S16.leg1, S18.leg1, S22.leg1, S23.leg1
  N11: Part1.D4, S15.leg1, S17.leg1, S19.leg1, S20.leg1, S21.leg1, S24.leg1
  N12: Part1.D5_PWM, S7.leg1, S8.leg1, S9.leg1, S10.leg1, S11.leg1, S12.leg1
  N13: Part1.D6_PWM, S1.leg1, S2.leg1, S3.leg1, S4.leg1, S5.leg1, S6.leg1
  N14: Part1.D7, S1.leg0, S9.leg0, S20.leg0, S22.leg0, S27.leg0
  N15: DFPlayer_Mini2.VCC, C1.+
  N16: DFPlayer_Mini2.SPK1, SP2.-
  N17: DFPlayer_Mini2.GND, C1.-
  N18: DFPlayer_Mini2.SPK2, SP2.+

custom parts:
  DFPlayer MINI: MP3 module by DFRobot.com for playing Music from an SD-Card. Supports WAV and MP3 files.
